# Fritzing sketch buttons (saved by Fritzing 0.8.7b)
circuit board: 6.56421cm x 5.52496cm
breadboards: 1

parts:
  R1 = Resistor [tolerance=±5% resistance=4.7k package=THT]
  R2 = Resistor [tolerance=±5% resistance=2.2k package=THT]
  S1 = Pushbutton [package="[THT]"]
  R3 = Resistor [tolerance=±5% resistance=1k package=THT]
  R4 = Resistor [tolerance=±5% resistance=680 package=THT]
  R5 = Resistor [tolerance=±5% resistance=470 package=THT]
  R6 = Resistor [tolerance=±5% resistance=10k package=THT]
  S2 = Pushbutton [package="[THT]"]
  S3 = Pushbutton [package="[THT]"]
  S4 = Pushbutton [package="[THT]"]
  S5 = Pushbutton [package="[THT]"]
  Componente1 = Arduino Micro (Rev3)

nets:
  N1: R1.Pin_0, S1.Pin_3, S1.Pin_4
  N2: R1.Pin_1, R2.Pin_1, R3.Pin_1, R4.Pin_1, R5.Pin_1, R6.Pin_1, Componente1.A0
  N3: R2.Pin_0, S2.Pin_3, S2.Pin_4
  N4: S1.Pin_1, S1.Pin_2, S2.Pin_1, S2.Pin_2, S3.Pin_1, S3.Pin_2, S4.Pin_1, S4.Pin_2, S5.Pin_1, S5.Pin_2, Componente1.5V
  N5: R3.Pin_0, S3.Pin_3, S3.Pin_4
  N6: R4.Pin_0, S4.Pin_3, S4.Pin_4
  N7: R5.Pin_0, S5.Pin_3, S5.Pin_4
  N8: R6.Pin_0, Componente1.GND
